// Logisim project gray-hex-start.circ as structural Verilog: 1 circuit, main circuit main
module main (
  input  G3,
  input  G2,
  input  G1,
  input  G0
);

  LED B2 (.in(G2));
  LED B3 (.in(G3));
  LED B0 (.in(G0));
  LED B1 (.in(G1));
  Hex_Digit_Display hex_digit_display_1 (.value({G3, G2, G1, G0}));  // open: dp
endmodule
