// Logisim project gray2.circ as structural Verilog: 1 circuit, main circuit main
module main (
  input  G3,
  input  G2,
  input  G1,
  input  G0
);

  wire [2:0] xor_3_out;

  LED B3 (.in(G3));
  LED B2 (.in(xor_3_out[2]));
  LED B1 (.in(xor_3_out[1]));
  LED B0 (.in(xor_3_out[0]));
  xor xor_1 (xor_3_out[2], G3, G2);
  xor xor_2 (xor_3_out[1], xor_3_out[2], G1);
  xor xor_3 (xor_3_out[0], xor_3_out[1], G0);
  Hex_Digit_Display hex_digit_display_1 (.value({G3, xor_3_out}));  // open: dp
endmodule
