// Logisim project truth1.circ as structural Verilog: 1 circuit, main circuit main
module main (
  input  A,
  input  B,
  input  C
);

  wire A___C_out, A_B_out, A_C___B_C_out, A_C_B_C_C_prime__A_B_out, B___C_out, C_prime__A_B_out, C_prime_out;

  or A_B (A_B_out, A, B);
  not C_prime (C_prime_out, C);
  and A___C (A___C_out, A, C);
  and B___C (B___C_out, B, C);
  or A_C___B_C (A_C___B_C_out, A___C_out, B___C_out);
  and C_prime__A_B (C_prime__A_B_out, A_B_out, C_prime_out);
  LED led_1 (.in(A_C_B_C_C_prime__A_B_out));
  or A_C_B_C_C_prime__A_B (A_C_B_C_C_prime__A_B_out, A_C___B_C_out, C_prime__A_B_out);
endmodule
